// Logisim project 1703008.circ as structural Verilog: 15 circuits, main circuit AND
module AND (
  input  [5:0] A,
  input  [5:0] B,
  output [5:0] O
);

  and and_1 (O[5], A[5], B[5]);
  and and_2 (O[4], A[4], B[4]);
  and and_3 (O[3], A[3], B[3]);
  and and_4 (O[2], A[2], B[2]);
  and and_5 (O[1], A[1], B[1]);
  and and_6 (O[0], A[0], B[0]);
endmodule

module FA (
  input  a,
  input  b,
  input  Cin,
  output S,
  output Cout
);

  wire and_1_out, and_2_out, xor_1_out;

  xor xor_1 (xor_1_out, a, b);
  xor xor_2 (S, xor_1_out, Cin);
  and and_1 (and_1_out, Cin, xor_1_out);
  and and_2 (and_2_out, a, b);
  or or_1 (Cout, and_1_out, and_2_out);
endmodule

module SUB (
  input  [5:0] A,
  input  [5:0] B,
  output [5:0] O,
  output out_4
);

  wire fa_2_cout, fa_3_cout, fa_4_cout, fa_5_cout, fa_6_cout, xor_1_out, xor_2_out, xor_3_out, xor_4_out,
       xor_5_out, xor_6_out;

  FA fa_1 (.a(A[5]), .b(xor_1_out), .S(O[5]), .Cin(fa_2_cout), .Cout(out_4));
  xor xor_1 (xor_1_out, B[5], 1'b1);
  xor xor_2 (xor_2_out, B[4], 1'b1);
  FA fa_2 (.a(A[4]), .b(xor_2_out), .S(O[4]), .Cin(fa_3_cout), .Cout(fa_2_cout));
  xor xor_3 (xor_3_out, B[3], 1'b1);
  FA fa_3 (.a(A[3]), .b(xor_3_out), .S(O[3]), .Cin(fa_4_cout), .Cout(fa_3_cout));
  xor xor_4 (xor_4_out, B[2], 1'b1);
  FA fa_4 (.a(A[2]), .b(xor_4_out), .S(O[2]), .Cin(fa_5_cout), .Cout(fa_4_cout));
  FA fa_5 (.a(A[1]), .b(xor_5_out), .S(O[1]), .Cin(fa_6_cout), .Cout(fa_5_cout));
  xor xor_5 (xor_5_out, B[1], 1'b1);
  xor xor_6 (xor_6_out, B[0], 1'b1);
  FA fa_6 (.a(A[0]), .b(xor_6_out), .S(O[0]), .Cin(1'b1), .Cout(fa_6_cout));

  // Other names for the same wires on the sheet: CF = out_4

  // Notes on the sheet:
  //   SEL
endmodule

module ALU (
  input  [5:0] A,
  input  [5:0] B,
  input  OP,
  output CF,
  output [5:0] R,
  output SF,
  output ZF
);

  wire or_1_out;
  wire [5:0] AND, SUB;

  AND and_1 (.A(A), .B(B), .O(AND));
  SUB sub_1 (.A(A), .B(B), .O(SUB), .out_4(CF));
  Multiplexer #(.width(6), .enable("false")) multiplexer_1 (.in0(AND), .in1(SUB), .out(R), .sel(OP));
  or or_1 (or_1_out, R[0], R[1], R[2], R[3], R[4], R[5]);
  not not_1 (ZF, or_1_out);

  assign SF = R[5];
endmodule

module _1_bit_Register (
  input  Din,
  input  Sel,
  input  Clock,
  output Dout
);

  wire multiplexer_1_out;

  Multiplexer #(.enable("false")) multiplexer_1 (.in0(Dout), .in1(Din), .out(multiplexer_1_out), .sel(Sel));
  D_Flip_Flop d_ff_1 (.clk(Clock), .D(multiplexer_1_out), .Q(Dout));  // open: Qn, preset, en, reset
endmodule

module _6_bit_Register (
  input  [5:0] Din_5_0,
  input  Sel,
  input  Clock,
  output [5:0] Dout_5_0
);

  _1_bit_Register u_1_bit_register_1 (.Din(Din_5_0[0]), .Sel(Sel), .Clock(Clock), .Dout(Dout_5_0[0]));
  _1_bit_Register u_1_bit_register_2 (.Din(Din_5_0[1]), .Sel(Sel), .Clock(Clock), .Dout(Dout_5_0[1]));
  _1_bit_Register u_1_bit_register_3 (.Din(Din_5_0[2]), .Sel(Sel), .Clock(Clock), .Dout(Dout_5_0[2]));
  _1_bit_Register u_1_bit_register_4 (.Din(Din_5_0[3]), .Sel(Sel), .Clock(Clock), .Dout(Dout_5_0[3]));
  _1_bit_Register u_1_bit_register_5 (.Din(Din_5_0[4]), .Sel(Sel), .Clock(Clock), .Dout(Dout_5_0[4]));
  _1_bit_Register u_1_bit_register_6 (.Din(Din_5_0[5]), .Sel(Sel), .Clock(Clock), .Dout(Dout_5_0[5]));
endmodule

module Register_Set (
  input  [5:0] WRD,
  input  WE,
  input  [1:0] WR,
  input  [1:0] RA,
  input  [1:0] RB,
  input  Clock,
  output [5:0] A,
  output [5:0] B
);

  wire decoder_1_out0, decoder_1_out1, decoder_1_out2;
  wire [5:0] R0, R1, R2;

  Decoder #(.select(2)) decoder_1 (
    .out0(decoder_1_out0), .out1(decoder_1_out1), .out2(decoder_1_out2), .sel(WR), .en(WE));  // open: out3
  _6_bit_Register u_6_bit_register_1 (.Din_5_0(WRD), .Sel(decoder_1_out0), .Clock(Clock), .Dout_5_0(R0));
  _6_bit_Register u_6_bit_register_2 (.Din_5_0(WRD), .Sel(decoder_1_out1), .Clock(Clock), .Dout_5_0(R1));
  _6_bit_Register u_6_bit_register_3 (.Din_5_0(WRD), .Sel(decoder_1_out2), .Clock(Clock), .Dout_5_0(R2));
  Multiplexer #(.select(2), .width(6), .enable("false")) multiplexer_1 (
    .in0(R0), .in1(R1), .in2(R2), .out(A), .sel(RA));  // open: in3
  Multiplexer #(.select(2), .width(6), .enable("false")) multiplexer_2 (
    .in0(R0), .in1(R1), .in2(R2), .out(B), .sel(RB));  // open: in3
endmodule

module _1x1_SRAM (
  input  Read_Select_1,
  input  Read_Select_2,
  input  Write_Data,
  input  Write_Select,
  input  Clock,
  output Read_Data_1,
  output Read_Data_2
);

  wire d_ff_1_q, multiplexer_1_out;

  Multiplexer #(.enable("false")) multiplexer_1 (
    .in0(d_ff_1_q), .in1(Write_Data), .out(multiplexer_1_out), .sel(Write_Select));
  D_Flip_Flop d_ff_1 (.clk(Clock), .D(multiplexer_1_out), .Q(d_ff_1_q));  // open: Qn, preset, en, reset
  and and_1 (Read_Data_1, Read_Select_1, d_ff_1_q);
  and and_2 (Read_Data_2, Read_Select_2, d_ff_1_q);
endmodule

module _1x18_SRAM (
  input  [17:0] Write_Data_17_0,
  input  Write_Select,
  input  Read_Select_1,
  input  Read_Select_2,
  input  Clock,
  output [17:0] Read_Data_1,
  output [17:0] Read_Data_2
);

  _1x1_SRAM u_1x1_sram_1 (
    .Read_Select_1(Read_Select_1), .Read_Select_2(Read_Select_2), .Write_Data(Write_Data_17_0[0]),
    .Write_Select(Write_Select), .Clock(Clock), .Read_Data_1(Read_Data_1[0]), .Read_Data_2(Read_Data_2[0]));
  _1x1_SRAM u_1x1_sram_2 (
    .Read_Select_1(Read_Select_1), .Read_Select_2(Read_Select_2), .Write_Data(Write_Data_17_0[6]),
    .Write_Select(Write_Select), .Clock(Clock), .Read_Data_1(Read_Data_1[6]), .Read_Data_2(Read_Data_2[6]));
  _1x1_SRAM u_1x1_sram_3 (
    .Read_Select_1(Read_Select_1), .Read_Select_2(Read_Select_2), .Write_Data(Write_Data_17_0[12]),
    .Write_Select(Write_Select), .Clock(Clock), .Read_Data_1(Read_Data_1[12]), .Read_Data_2(Read_Data_2[12]));
  _1x1_SRAM u_1x1_sram_4 (
    .Read_Select_1(Read_Select_1), .Read_Select_2(Read_Select_2), .Write_Data(Write_Data_17_0[1]),
    .Write_Select(Write_Select), .Clock(Clock), .Read_Data_1(Read_Data_1[1]), .Read_Data_2(Read_Data_2[1]));
  _1x1_SRAM u_1x1_sram_5 (
    .Read_Select_1(Read_Select_1), .Read_Select_2(Read_Select_2), .Write_Data(Write_Data_17_0[7]),
    .Write_Select(Write_Select), .Clock(Clock), .Read_Data_1(Read_Data_1[7]), .Read_Data_2(Read_Data_2[7]));
  _1x1_SRAM u_1x1_sram_6 (
    .Read_Select_1(Read_Select_1), .Read_Select_2(Read_Select_2), .Write_Data(Write_Data_17_0[13]),
    .Write_Select(Write_Select), .Clock(Clock), .Read_Data_1(Read_Data_1[13]), .Read_Data_2(Read_Data_2[13]));
  _1x1_SRAM u_1x1_sram_7 (
    .Read_Select_1(Read_Select_1), .Read_Select_2(Read_Select_2), .Write_Data(Write_Data_17_0[2]),
    .Write_Select(Write_Select), .Clock(Clock), .Read_Data_1(Read_Data_1[2]), .Read_Data_2(Read_Data_2[2]));
  _1x1_SRAM u_1x1_sram_8 (
    .Read_Select_1(Read_Select_1), .Read_Select_2(Read_Select_2), .Write_Data(Write_Data_17_0[8]),
    .Write_Select(Write_Select), .Clock(Clock), .Read_Data_1(Read_Data_1[8]), .Read_Data_2(Read_Data_2[8]));
  _1x1_SRAM u_1x1_sram_9 (
    .Read_Select_1(Read_Select_1), .Read_Select_2(Read_Select_2), .Write_Data(Write_Data_17_0[14]),
    .Write_Select(Write_Select), .Clock(Clock), .Read_Data_1(Read_Data_1[14]), .Read_Data_2(Read_Data_2[14]));
  _1x1_SRAM u_1x1_sram_10 (
    .Read_Select_1(Read_Select_1), .Read_Select_2(Read_Select_2), .Write_Data(Write_Data_17_0[3]),
    .Write_Select(Write_Select), .Clock(Clock), .Read_Data_1(Read_Data_1[3]), .Read_Data_2(Read_Data_2[3]));
  _1x1_SRAM u_1x1_sram_11 (
    .Read_Select_1(Read_Select_1), .Read_Select_2(Read_Select_2), .Write_Data(Write_Data_17_0[9]),
    .Write_Select(Write_Select), .Clock(Clock), .Read_Data_1(Read_Data_1[9]), .Read_Data_2(Read_Data_2[9]));
  _1x1_SRAM u_1x1_sram_12 (
    .Read_Select_1(Read_Select_1), .Read_Select_2(Read_Select_2), .Write_Data(Write_Data_17_0[15]),
    .Write_Select(Write_Select), .Clock(Clock), .Read_Data_1(Read_Data_1[15]), .Read_Data_2(Read_Data_2[15]));
  _1x1_SRAM u_1x1_sram_13 (
    .Read_Select_1(Read_Select_1), .Read_Select_2(Read_Select_2), .Write_Data(Write_Data_17_0[4]),
    .Write_Select(Write_Select), .Clock(Clock), .Read_Data_1(Read_Data_1[4]), .Read_Data_2(Read_Data_2[4]));
  _1x1_SRAM u_1x1_sram_14 (
    .Read_Select_1(Read_Select_1), .Read_Select_2(Read_Select_2), .Write_Data(Write_Data_17_0[10]),
    .Write_Select(Write_Select), .Clock(Clock), .Read_Data_1(Read_Data_1[10]), .Read_Data_2(Read_Data_2[10]));
  _1x1_SRAM u_1x1_sram_15 (
    .Read_Select_1(Read_Select_1), .Read_Select_2(Read_Select_2), .Write_Data(Write_Data_17_0[16]),
    .Write_Select(Write_Select), .Clock(Clock), .Read_Data_1(Read_Data_1[16]), .Read_Data_2(Read_Data_2[16]));
  _1x1_SRAM u_1x1_sram_16 (
    .Read_Select_1(Read_Select_1), .Read_Select_2(Read_Select_2), .Write_Data(Write_Data_17_0[5]),
    .Write_Select(Write_Select), .Clock(Clock), .Read_Data_1(Read_Data_1[5]), .Read_Data_2(Read_Data_2[5]));
  _1x1_SRAM u_1x1_sram_17 (
    .Read_Select_1(Read_Select_1), .Read_Select_2(Read_Select_2), .Write_Data(Write_Data_17_0[11]),
    .Write_Select(Write_Select), .Clock(Clock), .Read_Data_1(Read_Data_1[11]), .Read_Data_2(Read_Data_2[11]));
  _1x1_SRAM u_1x1_sram_18 (
    .Read_Select_1(Read_Select_1), .Read_Select_2(Read_Select_2), .Write_Data(Write_Data_17_0[17]),
    .Write_Select(Write_Select), .Clock(Clock), .Read_Data_1(Read_Data_1[17]), .Read_Data_2(Read_Data_2[17]));

  // Other names for the same wires on the sheet: CLK = Clock; RD1_0 = Read_Data_1[0]; RD1_1 = Read_Data_1[1];
  //   RD1_2 = Read_Data_1[2]; RD1_3 = Read_Data_1[3]; RD1_4 = Read_Data_1[4]; RD1_5 = Read_Data_1[5];
  //   RD1_6 = Read_Data_1[6]; RD1_7 = Read_Data_1[7]; RD1_8 = Read_Data_1[8]; RD1_9 = Read_Data_1[9];
  //   RD1_10 = Read_Data_1[10]; RD1_11 = Read_Data_1[11]; RD1_12 = Read_Data_1[12]; RD1_13 = Read_Data_1[13];
  //   RD1_14 = Read_Data_1[14]; RD1_15 = Read_Data_1[15]; RD1_16 = Read_Data_1[16]; RD1_17 = Read_Data_1[17];
  //   RD2_0 = Read_Data_2[0]; RD2_1 = Read_Data_2[1]; RD2_2 = Read_Data_2[2]; RD2_3 = Read_Data_2[3];
  //   RD2_4 = Read_Data_2[4]; RD2_5 = Read_Data_2[5]; RD2_6 = Read_Data_2[6]; RD2_7 = Read_Data_2[7];
  //   RD2_8 = Read_Data_2[8]; RD2_9 = Read_Data_2[9]; RD2_10 = Read_Data_2[10]; RD2_11 = Read_Data_2[11];
  //   RD2_12 = Read_Data_2[12]; RD2_13 = Read_Data_2[13]; RD2_14 = Read_Data_2[14]; RD2_15 = Read_Data_2[15];
  //   RD2_16 = Read_Data_2[16]; RD2_17 = Read_Data_2[17]; RS1 = Read_Select_1; RS2 = Read_Select_2;
  //   D0 = Write_Data_17_0[0]; D1 = Write_Data_17_0[1]; D2 = Write_Data_17_0[2]; D3 = Write_Data_17_0[3];
  //   D4 = Write_Data_17_0[4]; D5 = Write_Data_17_0[5]; D6 = Write_Data_17_0[6]; D7 = Write_Data_17_0[7];
  //   D8 = Write_Data_17_0[8]; D9 = Write_Data_17_0[9]; D10 = Write_Data_17_0[10]; D11 = Write_Data_17_0[11];
  //   D12 = Write_Data_17_0[12]; D13 = Write_Data_17_0[13]; D14 = Write_Data_17_0[14]; D15 = Write_Data_17_0[15];
  //   D16 = Write_Data_17_0[16]; D17 = Write_Data_17_0[17]; WS = Write_Select
endmodule

module _10x18_SRAM (
  input  [17:0] Write_Data_17_0,
  input  [3:0] Read_Address_1__3_0,
  input  [3:0] Read_Address_2__3_0,
  input  Write_Enable,
  input  [3:0] Write_Address__3_0,
  input  Clock,
  output [17:0] Read_Data_1,
  output [17:0] Read_Data_2
);

  wire R1_0, R1_1, R1_2, R1_3, R1_4, R1_5, R1_6, R1_7, R1_8, R1_9, R2_0, R2_1, R2_2, R2_3, R2_4, R2_5, R2_6,
       R2_7, R2_8, R2_9, W0, W1, W2, W3, W4, W5, W6, W7, W8, W9;
  wire [17:0] RD1_0, RD1_1, RD1_2, RD1_3, RD1_4, RD1_5, RD1_6, RD1_7, RD1_8, RD1_9, RD2_0, RD2_1, RD2_2,
       RD2_3, RD2_4, RD2_5, RD2_6, RD2_7, RD2_8, RD2_9;

  Decoder #(.select(4), .enable("false")) decoder_1 (
    .out0(R1_0), .out1(R1_1), .out2(R1_2), .out3(R1_3), .out4(R1_4), .out5(R1_5), .out6(R1_6), .out7(R1_7),
    .out8(R1_8), .out9(R1_9), .sel(Read_Address_1__3_0));  // open: out10, out11, out12, out13, out14, out15
  Decoder #(.select(4), .enable("false")) decoder_2 (
    .out0(R2_0), .out1(R2_1), .out2(R2_2), .out3(R2_3), .out4(R2_4), .out5(R2_5), .out6(R2_6), .out7(R2_7),
    .out8(R2_8), .out9(R2_9), .sel(Read_Address_2__3_0));  // open: out10, out11, out12, out13, out14, out15
  Decoder #(.select(4)) decoder_3 (
    .out0(W0), .out1(W1), .out2(W2), .out3(W3), .out4(W4), .out5(W5), .out6(W6), .out7(W7), .out8(W8),
    .out9(W9), .sel(Write_Address__3_0), .en(Write_Enable));  // open: out10, out11, out12, out13, out14, out15
  _1x18_SRAM u_1x18_sram_1 (
    .Write_Data_17_0(Write_Data_17_0), .Write_Select(W0), .Read_Select_1(R1_0), .Read_Select_2(R2_0),
    .Clock(Clock), .Read_Data_1(RD1_0), .Read_Data_2(RD2_0));
  _1x18_SRAM u_1x18_sram_2 (
    .Write_Data_17_0(Write_Data_17_0), .Write_Select(W1), .Read_Select_1(R1_1), .Read_Select_2(R2_1),
    .Clock(Clock), .Read_Data_1(RD1_1), .Read_Data_2(RD2_1));
  _1x18_SRAM u_1x18_sram_3 (
    .Write_Data_17_0(Write_Data_17_0), .Write_Select(W2), .Read_Select_1(R1_2), .Read_Select_2(R2_2),
    .Clock(Clock), .Read_Data_1(RD1_2), .Read_Data_2(RD2_2));
  _1x18_SRAM u_1x18_sram_4 (
    .Write_Data_17_0(Write_Data_17_0), .Write_Select(W3), .Read_Select_1(R1_3), .Read_Select_2(R2_3),
    .Clock(Clock), .Read_Data_1(RD1_3), .Read_Data_2(RD2_3));
  _1x18_SRAM u_1x18_sram_5 (
    .Write_Data_17_0(Write_Data_17_0), .Write_Select(W4), .Read_Select_1(R1_4), .Read_Select_2(R2_4),
    .Clock(Clock), .Read_Data_1(RD1_4), .Read_Data_2(RD2_4));
  _1x18_SRAM u_1x18_sram_6 (
    .Write_Data_17_0(Write_Data_17_0), .Write_Select(W5), .Read_Select_1(R1_5), .Read_Select_2(R2_5),
    .Clock(Clock), .Read_Data_1(RD1_5), .Read_Data_2(RD2_5));
  _1x18_SRAM u_1x18_sram_7 (
    .Write_Data_17_0(Write_Data_17_0), .Write_Select(W6), .Read_Select_1(R1_6), .Read_Select_2(R2_6),
    .Clock(Clock), .Read_Data_1(RD1_6), .Read_Data_2(RD2_6));
  _1x18_SRAM u_1x18_sram_8 (
    .Write_Data_17_0(Write_Data_17_0), .Write_Select(W7), .Read_Select_1(R1_7), .Read_Select_2(R2_7),
    .Clock(Clock), .Read_Data_1(RD1_7), .Read_Data_2(RD2_7));
  _1x18_SRAM u_1x18_sram_9 (
    .Write_Data_17_0(Write_Data_17_0), .Write_Select(W8), .Read_Select_1(R1_8), .Read_Select_2(R2_8),
    .Clock(Clock), .Read_Data_1(RD1_8), .Read_Data_2(RD2_8));
  _1x18_SRAM u_1x18_sram_10 (
    .Write_Data_17_0(Write_Data_17_0), .Write_Select(W9), .Read_Select_1(R1_9), .Read_Select_2(R2_9),
    .Clock(Clock), .Read_Data_1(RD1_9), .Read_Data_2(RD2_9));
  assign Read_Data_1 = RD1_0 | RD1_1 | RD1_2 | RD1_3 | RD1_4 | RD1_5 | RD1_6 | RD1_7 | RD1_8 | RD1_9;  // OR_Gate or_1, 18 bits wide
  assign Read_Data_2 = RD2_0 | RD2_1 | RD2_2 | RD2_3 | RD2_4 | RD2_5 | RD2_6 | RD2_7 | RD2_8 | RD2_9;  // OR_Gate or_2, 18 bits wide
endmodule

module CPU (
  input  [3:0] Write_Address__3_0,
  input  [17:0] Write_Data_17_0,
  input  Write_Enable,
  input  Clock,
  input  CPU_Enable
);

  wire alu_1_cf, alu_1_sf, alu_1_zf, CF, CPU_CLK, Imm_Sel, Jmp_Sel, Op, WE;
  wire [3:0] JMP_Addr, multiplexer_1_out, n4_bit_pc_adder_1_o_3_0, undriven;
  wire [5:0] alu_1_r, multiplexer_2_out, register_set_1_a, register_set_1_b;
  wire [17:0] n10x18_sram_1_read_data_1;

  Multiplexer #(.width(4), .disabled(0), .enable("false")) multiplexer_1 (
    .in0(undriven), .in1(JMP_Addr), .out(multiplexer_1_out), .sel(Jmp_Sel));
  and and_1 (CPU_CLK, Clock, CPU_Enable);
  _4_bit_PC_Adder u_4_bit_pc_adder_1 (.I__3_0(undriven), .O_3_0(n4_bit_pc_adder_1_o_3_0));
  _4_bit_Counter_Register u_4_bit_counter_register_1 (
    .Din_3_0(multiplexer_1_out), .Clock(CPU_CLK), .Dout_3_0(n4_bit_pc_adder_1_o_3_0));
  _10x18_SRAM u_10x18_sram_1 (
    .Write_Data_17_0(Write_Data_17_0), .Read_Address_1__3_0(n4_bit_pc_adder_1_o_3_0),
    .Write_Enable(Write_Enable), .Write_Address__3_0(Write_Address__3_0), .Clock(Clock),
    .Read_Data_1({n10x18_sram_1_read_data_1[17:15], JMP_Addr, n10x18_sram_1_read_data_1[10:0]}));  // open: Read_Address_2__3_0, Read_Data_2
  ALU alu_1 (
    .A(register_set_1_a), .B(multiplexer_2_out), .OP(Op), .CF(alu_1_cf), .R(alu_1_r), .SF(alu_1_sf),
    .ZF(alu_1_zf));
  Register_Set register_set_1 (
    .WRD(alu_1_r), .WE(WE), .WR(JMP_Addr[3:2]), .RA(JMP_Addr[3:2]), .RB(JMP_Addr[1:0]), .Clock(CPU_CLK),
    .A(register_set_1_a), .B(register_set_1_b));
  Multiplexer #(.width(6), .disabled(0), .enable("false")) multiplexer_2 (
    .in0(register_set_1_b), .in1({JMP_Addr[1:0], n10x18_sram_1_read_data_1[10:7]}), .out(multiplexer_2_out),
    .sel(Imm_Sel));
  Flag_Register flag_register_1 (
    .ZFin(alu_1_zf), .CFin(alu_1_cf), .SFin(alu_1_sf), .Clock(Clock), .CFout(CF));  // open: ZFout, SFout
  Control_Unit control_unit_1 (
    .Opcode__2_0(n10x18_sram_1_read_data_1[17:15]), .Op(Op), .Imm_Sel(Imm_Sel), .WE(WE), .CF(CF),
    .Jmp_Sel(Jmp_Sel));

  // Other names for the same wires on the sheet: CLK = Clock

  // Notes on the sheet:
  //   Branching Mode JNC = 100000100000000000
  //   Branching Mode: Opcode(2 bit+1 bit) + Address (4 bit) + Unused (11 bit) --> Opcode 1st 2bit = 10 + Opcode last bit = JNC(0)
  //   Register Mode: Opcode(2 bit+1 bit) + Register RA (2 bit) +  Register RB (2 bit) + Unused (11 bit) --> Opcode 1st 2bit = 00 + Opcode last bit = AND(0), SUB(1)
  //   Register Mode AND = 000001000000000000         Register Mode SUB = 001100000000000000
  //   Immediate Mode AND = 010100000100000000         Register Mode SUB = 011010000010000000
  //   Immediate Mode: Opcode(2 bit+1 bit) + Register RA (2 bit) +  Immediate Value(6 bit) + Unused (7 bit) --> Opcode 1st 2bit = 01 + Opcode last bit = AND(0), SUB(1)
endmodule

module _4_bit_Counter_Register (
  input  [3:0] Din_3_0,
  input  Clock,
  output [3:0] Dout_3_0
);

  _1_bit_Register u_1_bit_register_1 (.Din(Din_3_0[0]), .Sel(1'b1), .Clock(Clock), .Dout(Dout_3_0[0]));
  _1_bit_Register u_1_bit_register_2 (.Din(Din_3_0[1]), .Sel(1'b1), .Clock(Clock), .Dout(Dout_3_0[1]));
  _1_bit_Register u_1_bit_register_3 (.Din(Din_3_0[2]), .Sel(1'b1), .Clock(Clock), .Dout(Dout_3_0[2]));
  _1_bit_Register u_1_bit_register_4 (.Din(Din_3_0[3]), .Sel(1'b1), .Clock(Clock), .Dout(Dout_3_0[3]));
endmodule

module _4_bit_PC_Adder (
  input  [3:0] I__3_0,
  output [3:0] O_3_0
);

  wire [3:0] bit_extender_1_out;

  assign bit_extender_1_out = {{3{1'b0}}, 1'b1};  // Bit_Extender bit_extender_1
  Adder #(.width(4)) adder_1 (.a(I__3_0), .b(bit_extender_1_out), .out(O_3_0));  // open: cin, cout
endmodule

module Control_Unit (
  input  [2:0] Opcode__2_0,
  input  CF,
  output Op,
  output Imm_Sel,
  output WE,
  output Jmp_Sel
);

  wire not_1_out, not_2_out, not_3_out, not_4_out, not_5_out, Reg_out;

  not not_1 (not_1_out, Opcode__2_0[2]);
  not not_2 (not_2_out, Opcode__2_0[2]);
  not not_3 (not_3_out, Opcode__2_0[1]);
  not not_4 (not_4_out, Opcode__2_0[1]);
  not not_5 (not_5_out, CF);
  and Imm (Imm_Sel, not_1_out, Opcode__2_0[1]);
  and Reg (Reg_out, not_2_out, not_3_out);
  and Jnc (Jmp_Sel, Opcode__2_0[2], not_4_out, not_5_out);
  or or_1 (WE, Imm_Sel, Reg_out);

  assign Op = Opcode__2_0[0];
endmodule

module Flag_Register (
  input  ZFin,
  input  CFin,
  input  SFin,
  input  Clock,
  output ZFout,
  output CFout,
  output SFout
);

  _1_bit_Register u_1_bit_register_1 (.Din(ZFin), .Sel(1'b1), .Clock(Clock), .Dout(ZFout));
  _1_bit_Register u_1_bit_register_2 (.Din(CFin), .Sel(1'b1), .Clock(Clock), .Dout(CFout));
  _1_bit_Register u_1_bit_register_3 (.Din(SFin), .Sel(1'b1), .Clock(Clock), .Dout(SFout));
endmodule
